// Logisim project corg-final.circ as structural Verilog: 4 circuits, main circuit main
module main (
  output [15:0] out_1
);

  wire ADD, AND, and_1_out, and_2_out, and_3_out, and_4_out, and_5_out, and_6_out, and_7_out, and_8_out,
       and_9_out, and_10_out, and_11_out, and_12_out, and_13_out, and_14_out, and_15_out, and_16_out,
       and_17_out, and_18_out, and_19_out, and_20_out, and_21_out, and_22_out, and_23_out, and_24_out,
       and_25_out, and_26_out, and_27_out, and_28_out, and_29_out, and_30_out, and_31_out, and_32_out,
       and_33_out, and_34_out, and_35_out, and_36_out, and_37_out, and_38_out, and_39_out, and_40_out,
       and_41_out, and_42_out, and_43_out, and_44_out, and_45_out, and_46_out, and_47_out, and_48_out,
       and_49_out, and_50_out, and_51_out, and_52_out, and_53_out, and_54_out, and_55_out, and_56_out,
       clock_1_out, DEC, decoder_1_out0, decoder_8_out0, decoder_9_out0, decoder_9_out1, decoder_10_out0,
       decoder_10_out1, decoder_11_out0, decoder_11_out1, decoder_12_out0, decoder_12_out1, decoder_13_out0,
       decoder_13_out1, decoder_14_out0, decoder_14_out1, decoder_15_out0, decoder_15_out1, decoder_16_out0,
       decoder_16_out1, decoder_17_out0, decoder_17_out1, decoder_18_out0, decoder_18_out1, decoder_19_out0,
       decoder_19_out1, decoder_20_out0, decoder_20_out1, decoder_21_out0, decoder_21_out1, decoder_22_out0,
       decoder_29_out0, decoder_29_out1, decoder_30_out0, decoder_30_out1, decoder_31_out0, decoder_31_out1,
       decoder_32_out0, decoder_32_out1, decoder_33_out0, decoder_33_out1, decoder_34_out0, decoder_34_out1,
       decoder_36_out0, decoder_36_out1, decoder_37_out0, decoder_37_out1, decoder_38_out0, decoder_38_out1,
       decoder_39_out0, decoder_39_out1, DECSP, INC, INCSP, IR_EN, IR_LH, IRLTPC, IRTODST, LSSRC, MARTIRH,
       MARTIRL, MEM_CLR, MEM_LD, MEM_SEL, MEM_STR, MTDST, MuxCSel, NOT, not_1_out, not_2_out, not_3_out,
       not_4_out, not_5_out, not_6_out, not_7_out, not_8_out, not_9_out, not_10_out, not_11_out, not_12_out,
       not_13_out, not_14_out, not_15_out, not_16_out, not_17_out, not_18_out, not_19_out, not_20_out,
       not_21_out, not_22_out, not_23_out, not_24_out, not_25_out, not_26_out, not_27_out, not_28_out,
       not_29_out, not_30_out, not_31_out, not_32_out, not_33_out, not_34_out, not_35_out, not_36_out,
       not_37_out, not_38_out, not_39_out, not_40_out, OR, or_8_out, RSSRC, SPTSRC, SRCTDST, SRCTOM, SRCTSP,
       SUB, tunnel;
  wire [1:0] _3RB_FS, _4RB_FS, controlled_buffer_10_out, controlled_buffer_23_out, controlled_buffer_32_out,
       controlled_buffer_38_out, controlled_buffer_44_out, controlled_buffer_61_out,
       controlled_buffer_65_out, controlled_buffer_70_out, controlled_buffer_73_out,
       controlled_buffer_74_out, controlled_buffer_76_out, controlled_buffer_80_out,
       controlled_buffer_86_out, controlled_buffer_92_out, controlled_buffer_97_out,
       controlled_buffer_104_out, controlled_buffer_111_out, controlled_buffer_118_out,
       controlled_buffer_125_out, controlled_buffer_132_out, controlled_buffer_150_out,
       controlled_buffer_157_out, controlled_buffer_165_out, controlled_buffer_173_out,
       controlled_buffer_174_out, controlled_buffer_179_out, controlled_buffer_180_out,
       controlled_buffer_185_out, controlled_buffer_186_out, controlled_buffer_191_out,
       controlled_buffer_194_out, controlled_buffer_195_out, controlled_buffer_202_out,
       controlled_buffer_210_out, controlled_buffer_211_out, controlled_buffer_215_out,
       controlled_buffer_216_out, controlled_buffer_219_out, controlled_buffer_226_out,
       controlled_buffer_238_out, controlled_buffer_244_out, controlled_buffer_245_out,
       controlled_buffer_250_out, controlled_buffer_251_out, controlled_buffer_256_out,
       controlled_buffer_257_out, controlled_buffer_262_out, controlled_buffer_269_out,
       controlled_buffer_282_out, controlled_buffer_283_out, controlled_buffer_296_out,
       controlled_buffer_297_out, controlled_buffer_310_out, controlled_buffer_311_out,
       controlled_buffer_324_out, controlled_buffer_325_out, controlled_buffer_332_out,
       controlled_buffer_339_out, controlled_buffer_346_out, IR_FS, MuxASel, MuxBSel, OutASel, OutBSel,
       outcdecoder_4_out_2, outcdecoder_5_out_2, outcdecoder_6_out_2, outcdecoder_7_out_2,
       outcdecoder_8_out_2, outcdecoder_9_out_2, outcdecoder_10_out_2, outcdecoder_11_out_2,
       outcdecoder_20_out_2, outcdecoder_21_out_2, outcdecoder_22_out_2, outcdecoder_23_out_2,
       outcdecoder_24_out_2, outcdecoder_25_out_2, outcdecoder_26_out_2, outcdecoder_27_out_2, OutCSel,
       OutDSel;
  wire [2:0] F1, F2, F3;
  wire [3:0] _3RB_RS, _4RB_RS, ALUFlags, ALUFS;

  assign OutDSel = SRCTSP ? 2'b10 : 2'bz;  // Controlled_Buffer controlled_buffer_1
  assign MEM_SEL = SRCTSP ? 1'b1 : 1'bz;  // Controlled_Buffer controlled_buffer_2
  assign MEM_LD = SRCTSP ? 1'b1 : 1'bz;  // Controlled_Buffer controlled_buffer_3
  assign MEM_STR = SRCTSP ? 1'b1 : 1'bz;  // Controlled_Buffer controlled_buffer_4
  assign MEM_CLR = SRCTSP ? 1'b0 : 1'bz;  // Controlled_Buffer controlled_buffer_5
  Decoder #(.select(3), .enable("false")) decoder_1 (
    .out0(decoder_1_out0), .out1(SRCTDST), .out2(MTDST), .out3(IRTODST), .out4(INC), .out5(SUB), .out6(DEC),
    .out7(SRCTOM), .sel(F1));
  not not_1 (not_1_out, out_1[10]);
  and and_1 (and_1_out, SRCTDST, not_1_out, not_6_out);
  assign OutASel = and_1_out ? out_1[6:5] : 2'bz;  // Controlled_Buffer controlled_buffer_6
  assign MuxCSel = and_1_out ? 1'b1 : 1'bz;  // Controlled_Buffer controlled_buffer_7
  assign ALUFS = and_1_out ? 4'b0000 : 4'bz;  // Controlled_Buffer controlled_buffer_8
  assign MuxASel = and_1_out ? 2'b11 : 2'bz;  // Controlled_Buffer controlled_buffer_9
  Decoder #(.select(2)) decoder_2 (
    .out0(_4RB_RS[0]), .out1(_4RB_RS[1]), .out2(_4RB_RS[2]), .out3(_4RB_RS[3]),
    .sel(controlled_buffer_10_out), .en(and_1_out));
  assign controlled_buffer_10_out = and_1_out ? out_1[9:8] : 2'bz;  // Controlled_Buffer controlled_buffer_10
  assign _4RB_FS = and_1_out ? 2'b01 : 2'bz;  // Controlled_Buffer controlled_buffer_11
  assign IR_EN = MARTIRL ? 1'b1 : 1'bz;  // Controlled_Buffer controlled_buffer_12
  assign MEM_SEL = MARTIRL ? 1'b1 : 1'bz;  // Controlled_Buffer controlled_buffer_13
  assign MEM_LD = MARTIRL ? 1'b1 : 1'bz;  // Controlled_Buffer controlled_buffer_14
  assign IR_FS = MARTIRL ? 2'b11 : 2'bz;  // Controlled_Buffer controlled_buffer_15
  assign IR_LH = MARTIRL ? 1'b0 : 1'bz;  // Controlled_Buffer controlled_buffer_16
  assign OutDSel = MARTIRL ? 2'b00 : 2'bz;  // Controlled_Buffer controlled_buffer_17
  assign _3RB_FS = MARTIRL ? 2'b10 : 2'bz;  // Controlled_Buffer controlled_buffer_18
  assign _3RB_RS = MARTIRL ? 4'b0001 : 4'bz;  // Controlled_Buffer controlled_buffer_19
  assign MEM_STR = MARTIRL ? 1'b0 : 1'bz;  // Controlled_Buffer controlled_buffer_20
  assign MEM_CLR = MARTIRL ? 1'b0 : 1'bz;  // Controlled_Buffer controlled_buffer_21
  not not_2 (not_2_out, out_1[10]);
  and and_2 (and_2_out, INC, not_2_out);
  assign _4RB_FS = and_2_out ? 2'b10 : 2'bz;  // Controlled_Buffer controlled_buffer_22
  assign controlled_buffer_23_out = and_2_out ? out_1[9:8] : 2'bz;  // Controlled_Buffer controlled_buffer_23
  assign OutASel = and_2_out ? out_1[9:8] : 2'bz;  // Controlled_Buffer controlled_buffer_24
  assign MuxCSel = and_2_out ? 1'b1 : 1'bz;  // Controlled_Buffer controlled_buffer_25
  assign OutDSel = MTDST ? 2'b01 : 2'bz;  // Controlled_Buffer controlled_buffer_26
  assign MEM_SEL = MTDST ? 1'b1 : 1'bz;  // Controlled_Buffer controlled_buffer_27
  assign MEM_LD = MTDST ? 1'b1 : 1'bz;  // Controlled_Buffer controlled_buffer_28
  assign MEM_STR = MTDST ? 1'b0 : 1'bz;  // Controlled_Buffer controlled_buffer_29
  assign MEM_CLR = MTDST ? 1'b0 : 1'bz;  // Controlled_Buffer controlled_buffer_30
  not not_3 (not_3_out, out_1[7]);
  and and_3 (and_3_out, NOT, not_3_out, not_7_out);
  assign OutASel = and_3_out ? out_1[6:5] : 2'bz;  // Controlled_Buffer controlled_buffer_31
  assign controlled_buffer_32_out = and_3_out ? out_1[9:8] : 2'bz;  // Controlled_Buffer controlled_buffer_32
  assign MuxCSel = and_3_out ? 1'b1 : 1'bz;  // Controlled_Buffer controlled_buffer_33
  assign ALUFS = and_3_out ? 4'b0010 : 4'bz;  // Controlled_Buffer controlled_buffer_34
  assign MuxASel = and_3_out ? 2'b11 : 2'bz;  // Controlled_Buffer controlled_buffer_35
  assign _4RB_FS = and_3_out ? 2'b01 : 2'bz;  // Controlled_Buffer controlled_buffer_36
  not not_4 (not_4_out, out_1[7]);
  and and_4 (and_4_out, LSSRC, not_4_out, not_8_out);
  assign OutASel = and_4_out ? out_1[6:5] : 2'bz;  // Controlled_Buffer controlled_buffer_37
  assign controlled_buffer_38_out = and_4_out ? out_1[9:8] : 2'bz;  // Controlled_Buffer controlled_buffer_38
  assign MuxCSel = and_4_out ? 1'b1 : 1'bz;  // Controlled_Buffer controlled_buffer_39
  assign ALUFS = and_4_out ? 4'b1010 : 4'bz;  // Controlled_Buffer controlled_buffer_40
  assign MuxASel = and_4_out ? 2'b11 : 2'bz;  // Controlled_Buffer controlled_buffer_41
  assign _4RB_FS = and_4_out ? 2'b01 : 2'bz;  // Controlled_Buffer controlled_buffer_42
  not not_5 (not_5_out, out_1[7]);
  and and_5 (and_5_out, RSSRC, not_5_out, not_9_out);
  assign OutASel = and_5_out ? out_1[6:5] : 2'bz;  // Controlled_Buffer controlled_buffer_43
  assign controlled_buffer_44_out = and_5_out ? out_1[9:8] : 2'bz;  // Controlled_Buffer controlled_buffer_44
  assign MuxCSel = and_5_out ? 1'b1 : 1'bz;  // Controlled_Buffer controlled_buffer_45
  assign ALUFS = and_5_out ? 4'b1011 : 4'bz;  // Controlled_Buffer controlled_buffer_46
  assign MuxASel = and_5_out ? 2'b11 : 2'bz;  // Controlled_Buffer controlled_buffer_47
  assign _4RB_FS = and_5_out ? 2'b01 : 2'bz;  // Controlled_Buffer controlled_buffer_48
  Clock clock_1 (.out(clock_1_out));
  CONTROL_UNIT control_unit_1 (
    .in_2(out_1[8]), .NEGATIVE_FLAG(ALUFlags[2]), .ZERO_FLAG(ALUFlags[3]), .OPCODE(out_1[15:11]), .F1(F1),
    .F3(F3), .in_1(clock_1_out), .F2(F2));
  not not_6 (not_6_out, out_1[7]);
  Decoder #(.select(2)) decoder_3 (
    .out0(_4RB_RS[0]), .out1(_4RB_RS[1]), .out2(_4RB_RS[2]), .out3(_4RB_RS[3]),
    .sel(controlled_buffer_23_out), .en(and_2_out));
  and and_6 (and_6_out, SRCTSP, not_10_out);
  not not_7 (not_7_out, out_1[10]);
  Decoder #(.select(2)) decoder_4 (
    .out0(_4RB_RS[0]), .out1(_4RB_RS[1]), .out2(_4RB_RS[2]), .out3(_4RB_RS[3]),
    .sel(controlled_buffer_32_out), .en(and_3_out));
  not not_8 (not_8_out, out_1[10]);
  Decoder #(.select(2)) decoder_5 (
    .out0(_4RB_RS[0]), .out1(_4RB_RS[1]), .out2(_4RB_RS[2]), .out3(_4RB_RS[3]),
    .sel(controlled_buffer_38_out), .en(and_4_out));
  not not_9 (not_9_out, out_1[10]);
  Decoder #(.select(2)) decoder_6 (
    .out0(_4RB_RS[0]), .out1(_4RB_RS[1]), .out2(_4RB_RS[2]), .out3(_4RB_RS[3]),
    .sel(controlled_buffer_44_out), .en(and_5_out));
  assign IR_EN = MARTIRH ? 1'b1 : 1'bz;  // Controlled_Buffer controlled_buffer_49
  assign MEM_SEL = MARTIRH ? 1'b1 : 1'bz;  // Controlled_Buffer controlled_buffer_50
  assign MEM_LD = MARTIRH ? 1'b1 : 1'bz;  // Controlled_Buffer controlled_buffer_51
  assign IR_FS = MARTIRH ? 2'b11 : 2'bz;  // Controlled_Buffer controlled_buffer_52
  assign IR_LH = MARTIRH ? 1'b1 : 1'bz;  // Controlled_Buffer controlled_buffer_53
  assign OutDSel = MARTIRH ? 2'b00 : 2'bz;  // Controlled_Buffer controlled_buffer_54
  assign _3RB_FS = MARTIRH ? 2'b10 : 2'bz;  // Controlled_Buffer controlled_buffer_55
  assign _3RB_RS = MARTIRH ? 4'b0001 : 4'bz;  // Controlled_Buffer controlled_buffer_56
  assign MEM_STR = MARTIRH ? 1'b0 : 1'bz;  // Controlled_Buffer controlled_buffer_57
  assign MEM_CLR = MARTIRH ? 1'b0 : 1'bz;  // Controlled_Buffer controlled_buffer_58
  assign MuxASel = MTDST ? 2'b01 : 2'bz;  // Controlled_Buffer controlled_buffer_59
  assign _4RB_FS = MTDST ? 2'b01 : 2'bz;  // Controlled_Buffer controlled_buffer_60
  assign controlled_buffer_61_out = MTDST ? out_1[10:9] : 2'bz;  // Controlled_Buffer controlled_buffer_61
  not not_10 (not_10_out, out_1[10]);
  assign OutASel = and_6_out ? out_1[9:8] : 2'bz;  // Controlled_Buffer controlled_buffer_62
  assign MuxCSel = and_6_out ? 1'b1 : 1'bz;  // Controlled_Buffer controlled_buffer_63
  assign ALUFS = and_6_out ? 4'b0000 : 4'bz;  // Controlled_Buffer controlled_buffer_64
  and and_7 (and_7_out, ADD, out_1[10]);
  and and_8 (and_8_out, AND, out_1[10]);
  and and_9 (and_9_out, and_8_out, out_1[4]);
  and and_10 (and_10_out, OR, out_1[10]);
  and and_11 (and_11_out, and_10_out, out_1[4]);
  and and_12 (and_12_out, SUB, out_1[10]);
  and and_13 (and_13_out, SRCTDST, out_1[10], out_1[7]);
  assign controlled_buffer_65_out = and_13_out ? out_1[6:5] : 2'bz;  // Controlled_Buffer controlled_buffer_65
  assign MuxASel = and_13_out ? 2'b10 : 2'bz;  // Controlled_Buffer controlled_buffer_66
  assign MuxCSel = and_13_out ? 1'b0 : 1'bz;  // Controlled_Buffer controlled_buffer_67
  assign ALUFS = and_13_out ? 4'b0000 : 4'bz;  // Controlled_Buffer controlled_buffer_68
  assign MuxBSel = and_13_out ? 2'b11 : 2'bz;  // Controlled_Buffer controlled_buffer_69
  assign controlled_buffer_70_out = and_13_out ? out_1[9:8] : 2'bz;  // Controlled_Buffer controlled_buffer_70
  assign _3RB_FS = and_13_out ? 2'b01 : 2'bz;  // Controlled_Buffer controlled_buffer_71
  Decoder #(.select(2)) decoder_7 (
    .out0(_4RB_RS[0]), .out1(_4RB_RS[1]), .out2(_4RB_RS[2]), .out3(_4RB_RS[3]),
    .sel(controlled_buffer_61_out), .en(MTDST));
  not not_11 (not_11_out, out_1[7]);
  and and_14 (and_14_out, NOT, not_11_out, out_1[10]);
  not not_12 (not_12_out, out_1[7]);
  and and_15 (and_15_out, LSSRC, not_12_out, out_1[10]);
  and and_16 (and_16_out, and_7_out, out_1[7]);
  and and_17 (and_17_out, and_7_out, out_1[4]);
  and and_18 (and_18_out, and_8_out, out_1[7]);
  not not_13 (not_13_out, out_1[4]);
  and and_19 (and_19_out, and_10_out, out_1[7]);
  and and_20 (and_20_out, and_12_out, out_1[4]);
  Decoder #(.select(3), .enable("false")) decoder_8 (
    .out0(decoder_8_out0), .out1(ADD), .out2(AND), .out3(OR), .out4(NOT), .out5(LSSRC), .out6(RSSRC),
    .out7(tunnel), .sel(F2));
  outcdecoder outcdecoder_1 (.in_1(controlled_buffer_65_out), .out_2(OutCSel));
  Decoder #(.select(2), .disabled(0)) decoder_9 (
    .out0(decoder_9_out0), .out1(decoder_9_out1), .out2(_3RB_RS[1]), .out3(_3RB_RS[2]),
    .sel(controlled_buffer_70_out), .en(and_13_out));
  or or_1 (_3RB_RS[0], decoder_9_out0, decoder_9_out1);
  and and_21 (and_21_out, INC, out_1[10]);
  assign _3RB_FS = and_21_out ? 2'b10 : 2'bz;  // Controlled_Buffer controlled_buffer_72
  Decoder #(.select(2), .disabled(0)) decoder_10 (
    .out0(decoder_10_out0), .out1(decoder_10_out1), .out2(_3RB_RS[1]), .out3(_3RB_RS[2]),
    .sel(controlled_buffer_73_out), .en(and_21_out));
  assign controlled_buffer_73_out = and_21_out ? out_1[9:8] : 2'bz;  // Controlled_Buffer controlled_buffer_73
  or or_2 (_3RB_RS[0], decoder_10_out0, decoder_10_out1);
  assign controlled_buffer_74_out = and_21_out ? out_1[9:8] : 2'bz;  // Controlled_Buffer controlled_buffer_74
  outcdecoder outcdecoder_2 (.in_1(controlled_buffer_74_out), .out_2(OutCSel));
  assign MuxCSel = and_21_out ? 1'b0 : 1'bz;  // Controlled_Buffer controlled_buffer_75
  and and_22 (and_22_out, SRCTSP, out_1[10]);
  assign controlled_buffer_76_out = and_22_out ? out_1[9:8] : 2'bz;  // Controlled_Buffer controlled_buffer_76
  assign MuxCSel = and_22_out ? 1'b0 : 1'bz;  // Controlled_Buffer controlled_buffer_77
  assign ALUFS = and_22_out ? 4'b0000 : 4'bz;  // Controlled_Buffer controlled_buffer_78
  assign OutASel = and_14_out ? out_1[6:5] : 2'bz;  // Controlled_Buffer controlled_buffer_79
  Decoder #(.select(2), .disabled(0)) decoder_11 (
    .out0(decoder_11_out0), .out1(decoder_11_out1), .out2(_3RB_RS[1]), .out3(_3RB_RS[2]),
    .sel(controlled_buffer_80_out), .en(and_14_out));
  assign controlled_buffer_80_out = and_14_out ? out_1[9:8] : 2'bz;  // Controlled_Buffer controlled_buffer_80
  or or_3 (_3RB_RS[0], decoder_11_out0, decoder_11_out1);
  assign MuxCSel = and_14_out ? 1'b1 : 1'bz;  // Controlled_Buffer controlled_buffer_81
  assign ALUFS = and_14_out ? 4'b0010 : 4'bz;  // Controlled_Buffer controlled_buffer_82
  assign MuxBSel = and_14_out ? 2'b11 : 2'bz;  // Controlled_Buffer controlled_buffer_83
  assign _3RB_FS = and_14_out ? 2'b01 : 2'bz;  // Controlled_Buffer controlled_buffer_84
  assign OutASel = and_15_out ? out_1[6:5] : 2'bz;  // Controlled_Buffer controlled_buffer_85
  assign controlled_buffer_86_out = and_15_out ? out_1[9:8] : 2'bz;  // Controlled_Buffer controlled_buffer_86
  Decoder #(.select(2), .disabled(0)) decoder_12 (
    .out0(decoder_12_out0), .out1(decoder_12_out1), .out2(_3RB_RS[1]), .out3(_3RB_RS[2]),
    .sel(controlled_buffer_86_out), .en(and_15_out));
  or or_4 (_3RB_RS[0], decoder_12_out0, decoder_12_out1);
  assign MuxCSel = and_15_out ? 1'b1 : 1'bz;  // Controlled_Buffer controlled_buffer_87
  assign ALUFS = and_15_out ? 4'b1010 : 4'bz;  // Controlled_Buffer controlled_buffer_88
  assign MuxBSel = and_15_out ? 2'b11 : 2'bz;  // Controlled_Buffer controlled_buffer_89
  assign _3RB_FS = and_15_out ? 2'b01 : 2'bz;  // Controlled_Buffer controlled_buffer_90
  not not_14 (not_14_out, out_1[7]);
  and and_23 (and_23_out, RSSRC, not_14_out, out_1[10]);
  assign OutASel = and_23_out ? out_1[6:5] : 2'bz;  // Controlled_Buffer controlled_buffer_91
  assign controlled_buffer_92_out = and_23_out ? out_1[9:8] : 2'bz;  // Controlled_Buffer controlled_buffer_92
  assign MuxCSel = and_23_out ? 1'b1 : 1'bz;  // Controlled_Buffer controlled_buffer_93
  assign ALUFS = and_23_out ? 4'b1011 : 4'bz;  // Controlled_Buffer controlled_buffer_94
  assign MuxBSel = and_23_out ? 2'b11 : 2'bz;  // Controlled_Buffer controlled_buffer_95
  assign _3RB_FS = and_23_out ? 2'b01 : 2'bz;  // Controlled_Buffer controlled_buffer_96
  not not_15 (not_15_out, out_1[7]);
  not not_16 (not_16_out, out_1[4]);
  and and_24 (and_24_out, and_8_out, not_17_out, not_13_out);
  not not_17 (not_17_out, out_1[7]);
  not not_18 (not_18_out, out_1[7]);
  not not_19 (not_19_out, out_1[4]);
  and and_25 (and_25_out, and_12_out, out_1[7]);
  not not_20 (not_20_out, out_1[7]);
  not not_21 (not_21_out, out_1[4]);
  outcdecoder outcdecoder_3 (.in_1(controlled_buffer_76_out), .out_2(OutCSel));
  Decoder #(.select(2), .disabled(0)) decoder_13 (
    .out0(decoder_13_out0), .out1(decoder_13_out1), .out2(_3RB_RS[1]), .out3(_3RB_RS[2]),
    .sel(controlled_buffer_92_out), .en(and_23_out));
  or or_5 (_3RB_RS[0], decoder_13_out0, decoder_13_out1);
  assign controlled_buffer_97_out = and_16_out ? out_1[9:8] : 2'bz;  // Controlled_Buffer controlled_buffer_97
  assign _3RB_FS = and_16_out ? 2'b01 : 2'bz;  // Controlled_Buffer controlled_buffer_98
  assign MuxBSel = and_16_out ? 2'b11 : 2'bz;  // Controlled_Buffer controlled_buffer_99
  assign ALUFS = and_16_out ? 4'b0100 : 4'bz;  // Controlled_Buffer controlled_buffer_100
  assign OutBSel = and_16_out ? out_1[3:2] : 2'bz;  // Controlled_Buffer controlled_buffer_101
  outcdecoder outcdecoder_4 (.in_1(out_1[6:5]), .out_2(outcdecoder_4_out_2));
  assign OutCSel = and_16_out ? outcdecoder_4_out_2 : 2'bz;  // Controlled_Buffer controlled_buffer_102
  assign MuxCSel = and_16_out ? 1'b0 : 1'bz;  // Controlled_Buffer controlled_buffer_103
  and and_26 (and_26_out, and_7_out, not_15_out, not_16_out);
  assign controlled_buffer_104_out = and_17_out ? out_1[9:8] : 2'bz;  // Controlled_Buffer controlled_buffer_104
  assign _3RB_FS = and_17_out ? 2'b01 : 2'bz;  // Controlled_Buffer controlled_buffer_105
  assign MuxBSel = and_17_out ? 2'b11 : 2'bz;  // Controlled_Buffer controlled_buffer_106
  assign ALUFS = and_17_out ? 4'b0100 : 4'bz;  // Controlled_Buffer controlled_buffer_107
  assign OutBSel = and_17_out ? out_1[6:5] : 2'bz;  // Controlled_Buffer controlled_buffer_108
  outcdecoder outcdecoder_5 (.in_1(out_1[3:2]), .out_2(outcdecoder_5_out_2));
  assign OutCSel = and_17_out ? outcdecoder_5_out_2 : 2'bz;  // Controlled_Buffer controlled_buffer_109
  assign MuxCSel = and_17_out ? 1'b0 : 1'bz;  // Controlled_Buffer controlled_buffer_110
  Decoder #(.select(2), .disabled(0)) decoder_14 (
    .out0(decoder_14_out0), .out1(decoder_14_out1), .out2(_3RB_RS[1]), .out3(_3RB_RS[2]),
    .sel(controlled_buffer_111_out), .en(and_18_out));
  assign controlled_buffer_111_out = and_18_out ? out_1[9:8] : 2'bz;  // Controlled_Buffer controlled_buffer_111
  or or_6 (_3RB_RS[0], decoder_14_out0, decoder_14_out1);
  assign _3RB_FS = and_18_out ? 2'b01 : 2'bz;  // Controlled_Buffer controlled_buffer_112
  assign MuxBSel = and_18_out ? 2'b11 : 2'bz;  // Controlled_Buffer controlled_buffer_113
  assign ALUFS = and_18_out ? 4'b0111 : 4'bz;  // Controlled_Buffer controlled_buffer_114
  assign OutBSel = and_18_out ? out_1[3:2] : 2'bz;  // Controlled_Buffer controlled_buffer_115
  outcdecoder outcdecoder_6 (.in_1(out_1[6:5]), .out_2(outcdecoder_6_out_2));
  assign OutCSel = and_18_out ? outcdecoder_6_out_2 : 2'bz;  // Controlled_Buffer controlled_buffer_116
  assign MuxCSel = and_18_out ? 1'b0 : 1'bz;  // Controlled_Buffer controlled_buffer_117
  Decoder #(.select(2), .disabled(0)) decoder_15 (
    .out0(decoder_15_out0), .out1(decoder_15_out1), .out2(_3RB_RS[1]), .out3(_3RB_RS[2]),
    .sel(controlled_buffer_118_out), .en(and_9_out));
  assign controlled_buffer_118_out = and_9_out ? out_1[9:8] : 2'bz;  // Controlled_Buffer controlled_buffer_118
  or or_7 (_3RB_RS[0], decoder_15_out0, decoder_15_out1);
  assign _3RB_FS = and_9_out ? 2'b01 : 2'bz;  // Controlled_Buffer controlled_buffer_119
  assign MuxBSel = and_9_out ? 2'b11 : 2'bz;  // Controlled_Buffer controlled_buffer_120
  assign ALUFS = and_9_out ? 4'b0111 : 4'bz;  // Controlled_Buffer controlled_buffer_121
  assign OutBSel = and_9_out ? out_1[6:5] : 2'bz;  // Controlled_Buffer controlled_buffer_122
  assign OutCSel = and_9_out ? outcdecoder_7_out_2 : 2'bz;  // Controlled_Buffer controlled_buffer_123
  outcdecoder outcdecoder_7 (.in_1(out_1[3:2]), .out_2(outcdecoder_7_out_2));
  assign MuxCSel = and_9_out ? 1'b0 : 1'bz;  // Controlled_Buffer controlled_buffer_124
  assign controlled_buffer_125_out = and_19_out ? out_1[9:8] : 2'bz;  // Controlled_Buffer controlled_buffer_125
  assign _3RB_FS = and_19_out ? 2'b01 : 2'bz;  // Controlled_Buffer controlled_buffer_126
  assign MuxBSel = and_19_out ? 2'b11 : 2'bz;  // Controlled_Buffer controlled_buffer_127
  assign ALUFS = and_19_out ? 4'b1000 : 4'bz;  // Controlled_Buffer controlled_buffer_128
  assign OutBSel = and_19_out ? out_1[3:2] : 2'bz;  // Controlled_Buffer controlled_buffer_129
  assign OutCSel = and_19_out ? outcdecoder_8_out_2 : 2'bz;  // Controlled_Buffer controlled_buffer_130
  outcdecoder outcdecoder_8 (.in_1(out_1[6:5]), .out_2(outcdecoder_8_out_2));
  assign MuxCSel = and_19_out ? 1'b0 : 1'bz;  // Controlled_Buffer controlled_buffer_131
  and and_27 (and_27_out, and_10_out, not_18_out, not_19_out);
  assign controlled_buffer_132_out = and_11_out ? out_1[9:8] : 2'bz;  // Controlled_Buffer controlled_buffer_132
  assign _3RB_FS = and_11_out ? 2'b01 : 2'bz;  // Controlled_Buffer controlled_buffer_133
  assign MuxBSel = and_11_out ? 2'b11 : 2'bz;  // Controlled_Buffer controlled_buffer_134
  assign ALUFS = and_11_out ? 4'b1000 : 4'bz;  // Controlled_Buffer controlled_buffer_135
  assign OutBSel = and_11_out ? out_1[6:5] : 2'bz;  // Controlled_Buffer controlled_buffer_136
  assign OutCSel = and_11_out ? outcdecoder_9_out_2 : 2'bz;  // Controlled_Buffer controlled_buffer_137
  outcdecoder outcdecoder_9 (.in_1(out_1[3:2]), .out_2(outcdecoder_9_out_2));
  assign MuxCSel = and_11_out ? 1'b0 : 1'bz;  // Controlled_Buffer controlled_buffer_138
  outcdecoder outcdecoder_10 (.in_1(out_1[6:5]), .out_2(outcdecoder_10_out_2));
  and and_28 (and_28_out, and_12_out, not_20_out, not_21_out);
  outcdecoder outcdecoder_11 (.in_1(out_1[3:2]), .out_2(outcdecoder_11_out_2));
  or or_8 (or_8_out, SUB, OR, INC, DEC, NOT, LSSRC, RSSRC, AND, ADD);
  assign MEM_SEL = or_8_out ? 1'b0 : 1'bz;  // Controlled_Buffer controlled_buffer_139
  assign MEM_LD = or_8_out ? 1'b0 : 1'bz;  // Controlled_Buffer controlled_buffer_140
  assign MEM_STR = or_8_out ? 1'b0 : 1'bz;  // Controlled_Buffer controlled_buffer_141
  assign MEM_CLR = or_8_out ? 1'b0 : 1'bz;  // Controlled_Buffer controlled_buffer_142
  and and_29 (and_29_out, DEC, not_22_out);
  assign OutBSel = SRCTOM ? out_1[10:9] : 2'bz;  // Controlled_Buffer controlled_buffer_143
  assign ALUFS = SRCTOM ? 4'b0001 : 4'bz;  // Controlled_Buffer controlled_buffer_144
  assign MEM_SEL = SRCTOM ? 1'b1 : 1'bz;  // Controlled_Buffer controlled_buffer_145
  assign MEM_LD = SRCTOM ? 1'b1 : 1'bz;  // Controlled_Buffer controlled_buffer_146
  assign MEM_STR = SRCTOM ? 1'b1 : 1'bz;  // Controlled_Buffer controlled_buffer_147
  assign MEM_CLR = SRCTOM ? 1'b0 : 1'bz;  // Controlled_Buffer controlled_buffer_148
  assign OutDSel = SRCTOM ? 2'b01 : 2'bz;  // Controlled_Buffer controlled_buffer_149
  Decoder #(.select(2), .disabled(0)) decoder_16 (
    .out0(decoder_16_out0), .out1(decoder_16_out1), .out2(_3RB_RS[1]), .out3(_3RB_RS[2]),
    .sel(controlled_buffer_97_out), .en(and_16_out));
  or or_9 (_3RB_RS[0], decoder_16_out0, decoder_16_out1);
  Decoder #(.select(2), .disabled(0)) decoder_17 (
    .out0(decoder_17_out0), .out1(decoder_17_out1), .out2(_3RB_RS[1]), .out3(_3RB_RS[2]),
    .sel(controlled_buffer_104_out), .en(and_17_out));
  or or_10 (_3RB_RS[0], decoder_17_out0, decoder_17_out1);
  Decoder #(.select(2), .disabled(0)) decoder_18 (
    .out0(decoder_18_out0), .out1(decoder_18_out1), .out2(_3RB_RS[1]), .out3(_3RB_RS[2]),
    .sel(controlled_buffer_125_out), .en(and_19_out));
  or or_11 (_3RB_RS[0], decoder_18_out0, decoder_18_out1);
  Decoder #(.select(2), .disabled(0)) decoder_19 (
    .out0(decoder_19_out0), .out1(decoder_19_out1), .out2(_3RB_RS[1]), .out3(_3RB_RS[2]),
    .sel(controlled_buffer_132_out), .en(and_11_out));
  or or_12 (_3RB_RS[0], decoder_19_out0, decoder_19_out1);
  assign controlled_buffer_150_out = and_25_out ? out_1[9:8] : 2'bz;  // Controlled_Buffer controlled_buffer_150
  Decoder #(.select(2), .disabled(0)) decoder_20 (
    .out0(decoder_20_out0), .out1(decoder_20_out1), .out2(_3RB_RS[1]), .out3(_3RB_RS[2]),
    .sel(controlled_buffer_150_out), .en(and_25_out));
  or or_13 (_3RB_RS[0], decoder_20_out0, decoder_20_out1);
  assign _3RB_FS = and_25_out ? 2'b01 : 2'bz;  // Controlled_Buffer controlled_buffer_151
  assign MuxBSel = and_25_out ? 2'b11 : 2'bz;  // Controlled_Buffer controlled_buffer_152
  assign ALUFS = and_25_out ? 4'b0110 : 4'bz;  // Controlled_Buffer controlled_buffer_153
  assign OutBSel = and_25_out ? out_1[3:2] : 2'bz;  // Controlled_Buffer controlled_buffer_154
  assign OutCSel = and_25_out ? outcdecoder_10_out_2 : 2'bz;  // Controlled_Buffer controlled_buffer_155
  assign MuxCSel = and_25_out ? 1'b0 : 1'bz;  // Controlled_Buffer controlled_buffer_156
  assign controlled_buffer_157_out = and_20_out ? out_1[9:8] : 2'bz;  // Controlled_Buffer controlled_buffer_157
  Decoder #(.select(2), .disabled(0)) decoder_21 (
    .out0(decoder_21_out0), .out1(decoder_21_out1), .out2(_3RB_RS[1]), .out3(_3RB_RS[2]),
    .sel(controlled_buffer_157_out), .en(and_20_out));
  or or_14 (_3RB_RS[0], decoder_21_out0, decoder_21_out1);
  assign _3RB_FS = and_20_out ? 2'b01 : 2'bz;  // Controlled_Buffer controlled_buffer_158
  assign MuxBSel = and_20_out ? 2'b11 : 2'bz;  // Controlled_Buffer controlled_buffer_159
  assign ALUFS = and_20_out ? 4'b0110 : 4'bz;  // Controlled_Buffer controlled_buffer_160
  assign OutBSel = and_20_out ? out_1[6:5] : 2'bz;  // Controlled_Buffer controlled_buffer_161
  assign OutCSel = and_20_out ? outcdecoder_11_out_2 : 2'bz;  // Controlled_Buffer controlled_buffer_162
  assign MuxCSel = and_20_out ? 1'b0 : 1'bz;  // Controlled_Buffer controlled_buffer_163
  part2_edited_main main_1 (
    .OutASel(OutASel), .OutBSel(OutBSel), .FunSel_2(_4RB_FS), .RegSel(_4RB_RS), .MuxASel(MuxASel),
    .OutCSel(OutCSel), .OutDSel(OutDSel), .FunSel_3(_3RB_FS), .RegSel_2(_3RB_RS), .L_H(IR_LH),
    .Enable(IR_EN), .FunSel_4(IR_FS), .MuxCSel(MuxCSel), .MuxBSel(MuxBSel), .FunSel(ALUFS), .in_10(MEM_STR),
    .in_11(MEM_SEL), .in_12(MEM_LD), .in_13(MEM_CLR), .out_22(ALUFlags), .out_23(out_1), .in_2(clock_1_out));  // open: out_21
  Decoder #(.select(3), .enable("false")) decoder_22 (
    .out0(decoder_22_out0), .out1(MARTIRL), .out2(MARTIRH), .out3(SRCTSP), .out4(SPTSRC), .out5(IRLTPC),
    .out6(INCSP), .out7(DECSP), .sel(F3));
  not not_22 (not_22_out, out_1[10]);
  assign _4RB_FS = and_29_out ? 2'b11 : 2'bz;  // Controlled_Buffer controlled_buffer_164
  Decoder #(.select(2)) decoder_23 (
    .out0(_4RB_RS[0]), .out1(_4RB_RS[1]), .out2(_4RB_RS[2]), .out3(_4RB_RS[3]),
    .sel(controlled_buffer_165_out), .en(and_29_out));
  assign controlled_buffer_165_out = and_29_out ? out_1[9:8] : 2'bz;  // Controlled_Buffer controlled_buffer_165
  assign OutASel = and_29_out ? out_1[9:8] : 2'bz;  // Controlled_Buffer controlled_buffer_166
  assign MuxCSel = and_29_out ? 1'b1 : 1'bz;  // Controlled_Buffer controlled_buffer_167
  assign OutDSel = SPTSRC ? 2'b10 : 2'bz;  // Controlled_Buffer controlled_buffer_168
  assign MEM_SEL = SPTSRC ? 1'b1 : 1'bz;  // Controlled_Buffer controlled_buffer_169
  assign MEM_LD = SPTSRC ? 1'b1 : 1'bz;  // Controlled_Buffer controlled_buffer_170
  assign MEM_STR = SPTSRC ? 1'b0 : 1'bz;  // Controlled_Buffer controlled_buffer_171
  assign MEM_CLR = SPTSRC ? 1'b0 : 1'bz;  // Controlled_Buffer controlled_buffer_172
  and and_30 (and_30_out, NOT, out_1[7], not_24_out);
  outcdecoder outcdecoder_12 (.in_1(controlled_buffer_173_out), .out_2(OutCSel));
  assign controlled_buffer_173_out = and_30_out ? out_1[6:5] : 2'bz;  // Controlled_Buffer controlled_buffer_173
  Decoder #(.select(2)) decoder_24 (
    .out0(_4RB_RS[0]), .out1(_4RB_RS[1]), .out2(_4RB_RS[2]), .out3(_4RB_RS[3]),
    .sel(controlled_buffer_174_out), .en(and_30_out));
  assign controlled_buffer_174_out = and_30_out ? out_1[9:8] : 2'bz;  // Controlled_Buffer controlled_buffer_174
  assign MuxCSel = and_30_out ? 1'b0 : 1'bz;  // Controlled_Buffer controlled_buffer_175
  assign ALUFS = and_30_out ? 4'b0010 : 4'bz;  // Controlled_Buffer controlled_buffer_176
  assign MuxASel = and_30_out ? 2'b11 : 2'bz;  // Controlled_Buffer controlled_buffer_177
  assign _4RB_FS = and_30_out ? 2'b01 : 2'bz;  // Controlled_Buffer controlled_buffer_178
  and and_31 (and_31_out, LSSRC, out_1[7], not_25_out);
  outcdecoder outcdecoder_13 (.in_1(controlled_buffer_179_out), .out_2(OutCSel));
  assign controlled_buffer_179_out = and_31_out ? out_1[6:5] : 2'bz;  // Controlled_Buffer controlled_buffer_179
  Decoder #(.select(2)) decoder_25 (
    .out0(_4RB_RS[0]), .out1(_4RB_RS[1]), .out2(_4RB_RS[2]), .out3(_4RB_RS[3]),
    .sel(controlled_buffer_180_out), .en(and_31_out));
  assign controlled_buffer_180_out = and_31_out ? out_1[9:8] : 2'bz;  // Controlled_Buffer controlled_buffer_180
  assign MuxCSel = and_31_out ? 1'b0 : 1'bz;  // Controlled_Buffer controlled_buffer_181
  assign ALUFS = and_31_out ? 4'b1010 : 4'bz;  // Controlled_Buffer controlled_buffer_182
  assign MuxASel = and_31_out ? 2'b11 : 2'bz;  // Controlled_Buffer controlled_buffer_183
  assign _4RB_FS = and_31_out ? 2'b01 : 2'bz;  // Controlled_Buffer controlled_buffer_184
  and and_32 (and_32_out, RSSRC, out_1[7], not_26_out);
  assign controlled_buffer_185_out = and_32_out ? out_1[6:5] : 2'bz;  // Controlled_Buffer controlled_buffer_185
  Decoder #(.select(2)) decoder_26 (
    .out0(_4RB_RS[0]), .out1(_4RB_RS[1]), .out2(_4RB_RS[2]), .out3(_4RB_RS[3]),
    .sel(controlled_buffer_186_out), .en(and_32_out));
  assign controlled_buffer_186_out = and_32_out ? out_1[9:8] : 2'bz;  // Controlled_Buffer controlled_buffer_186
  assign MuxCSel = and_32_out ? 1'b0 : 1'bz;  // Controlled_Buffer controlled_buffer_187
  assign ALUFS = and_32_out ? 4'b1011 : 4'bz;  // Controlled_Buffer controlled_buffer_188
  assign MuxASel = and_32_out ? 2'b11 : 2'bz;  // Controlled_Buffer controlled_buffer_189
  assign _4RB_FS = and_32_out ? 2'b01 : 2'bz;  // Controlled_Buffer controlled_buffer_190
  not not_23 (not_23_out, out_1[10]);
  and and_33 (and_33_out, SRCTDST, not_23_out, out_1[7]);
  assign controlled_buffer_191_out = and_33_out ? out_1[6:5] : 2'bz;  // Controlled_Buffer controlled_buffer_191
  assign MuxASel = and_33_out ? 2'b10 : 2'bz;  // Controlled_Buffer controlled_buffer_192
  assign _4RB_FS = and_33_out ? 2'b01 : 2'bz;  // Controlled_Buffer controlled_buffer_193
  Decoder #(.select(2)) decoder_27 (
    .out0(_4RB_RS[0]), .out1(_4RB_RS[1]), .out2(_4RB_RS[2]), .out3(_4RB_RS[3]),
    .sel(controlled_buffer_194_out), .en(and_33_out));
  assign controlled_buffer_194_out = and_33_out ? out_1[9:8] : 2'bz;  // Controlled_Buffer controlled_buffer_194
  not not_24 (not_24_out, out_1[10]);
  not not_25 (not_25_out, out_1[10]);
  not not_26 (not_26_out, out_1[10]);
  outcdecoder outcdecoder_14 (.in_1(controlled_buffer_185_out), .out_2(OutCSel));
  Hex_Digit_Display hex_digit_display_1 (.value(out_1[15:12]));  // open: dp
  outcdecoder outcdecoder_15 (.in_1(controlled_buffer_191_out), .out_2(OutCSel));
  and and_34 (and_34_out, SPTSRC, not_27_out);
  assign controlled_buffer_195_out = and_24_out ? out_1[9:8] : 2'bz;  // Controlled_Buffer controlled_buffer_195
  assign _3RB_FS = and_24_out ? 2'b01 : 2'bz;  // Controlled_Buffer controlled_buffer_196
  assign MuxBSel = and_24_out ? 2'b11 : 2'bz;  // Controlled_Buffer controlled_buffer_197
  assign ALUFS = and_24_out ? 4'b0111 : 4'bz;  // Controlled_Buffer controlled_buffer_198
  assign OutBSel = and_24_out ? out_1[3:2] : 2'bz;  // Controlled_Buffer controlled_buffer_199
  assign MuxCSel = and_24_out ? 1'b1 : 1'bz;  // Controlled_Buffer controlled_buffer_200
  assign OutASel = and_24_out ? out_1[6:5] : 2'bz;  // Controlled_Buffer controlled_buffer_201
  assign controlled_buffer_202_out = and_27_out ? out_1[9:8] : 2'bz;  // Controlled_Buffer controlled_buffer_202
  assign _3RB_FS = and_27_out ? 2'b01 : 2'bz;  // Controlled_Buffer controlled_buffer_203
  assign MuxBSel = and_27_out ? 2'b11 : 2'bz;  // Controlled_Buffer controlled_buffer_204
  assign ALUFS = and_27_out ? 4'b1000 : 4'bz;  // Controlled_Buffer controlled_buffer_205
  assign OutBSel = and_27_out ? out_1[3:2] : 2'bz;  // Controlled_Buffer controlled_buffer_206
  assign MuxCSel = and_27_out ? 1'b1 : 1'bz;  // Controlled_Buffer controlled_buffer_207
  assign OutASel = and_27_out ? out_1[6:5] : 2'bz;  // Controlled_Buffer controlled_buffer_208
  Hex_Digit_Display hex_digit_display_2 (.value(out_1[11:8]));  // open: dp
  Hex_Digit_Display hex_digit_display_3 (.value(out_1[7:4]));  // open: dp
  and and_35 (and_35_out, DEC, out_1[10]);
  assign _3RB_FS = and_35_out ? 2'b11 : 2'bz;  // Controlled_Buffer controlled_buffer_209
  assign controlled_buffer_210_out = and_35_out ? out_1[9:8] : 2'bz;  // Controlled_Buffer controlled_buffer_210
  assign controlled_buffer_211_out = and_35_out ? out_1[9:8] : 2'bz;  // Controlled_Buffer controlled_buffer_211
  assign MuxCSel = and_35_out ? 1'b0 : 1'bz;  // Controlled_Buffer controlled_buffer_212
  assign MuxASel = IRTODST ? 2'b00 : 2'bz;  // Controlled_Buffer controlled_buffer_213
  assign _4RB_FS = IRTODST ? 2'b01 : 2'bz;  // Controlled_Buffer controlled_buffer_214
  assign controlled_buffer_215_out = IRTODST ? out_1[10:9] : 2'bz;  // Controlled_Buffer controlled_buffer_215
  not not_27 (not_27_out, out_1[10]);
  Decoder #(.select(2)) decoder_28 (
    .out0(_4RB_RS[0]), .out1(_4RB_RS[1]), .out2(_4RB_RS[2]), .out3(_4RB_RS[3]),
    .sel(controlled_buffer_216_out), .en(and_34_out));
  assign controlled_buffer_216_out = and_34_out ? out_1[9:8] : 2'bz;  // Controlled_Buffer controlled_buffer_216
  assign _4RB_FS = and_34_out ? 2'b01 : 2'bz;  // Controlled_Buffer controlled_buffer_217
  assign MuxASel = and_34_out ? 2'b01 : 2'bz;  // Controlled_Buffer controlled_buffer_218
  assign controlled_buffer_219_out = and_26_out ? out_1[9:8] : 2'bz;  // Controlled_Buffer controlled_buffer_219
  Decoder #(.select(2), .disabled(0)) decoder_29 (
    .out0(decoder_29_out0), .out1(decoder_29_out1), .out2(_3RB_RS[1]), .out3(_3RB_RS[2]),
    .sel(controlled_buffer_219_out), .en(and_26_out));
  or or_15 (_3RB_RS[0], decoder_29_out0, decoder_29_out1);
  assign _3RB_FS = and_26_out ? 2'b01 : 2'bz;  // Controlled_Buffer controlled_buffer_220
  assign MuxBSel = and_26_out ? 2'b11 : 2'bz;  // Controlled_Buffer controlled_buffer_221
  assign ALUFS = and_26_out ? 4'b0100 : 4'bz;  // Controlled_Buffer controlled_buffer_222
  assign OutBSel = and_26_out ? out_1[3:2] : 2'bz;  // Controlled_Buffer controlled_buffer_223
  assign MuxCSel = and_26_out ? 1'b1 : 1'bz;  // Controlled_Buffer controlled_buffer_224
  assign OutASel = and_26_out ? out_1[6:5] : 2'bz;  // Controlled_Buffer controlled_buffer_225
  Decoder #(.select(2), .disabled(0)) decoder_30 (
    .out0(decoder_30_out0), .out1(decoder_30_out1), .out2(_3RB_RS[1]), .out3(_3RB_RS[2]),
    .sel(controlled_buffer_195_out), .en(and_24_out));
  or or_16 (_3RB_RS[0], decoder_30_out0, decoder_30_out1);
  Decoder #(.select(2), .disabled(0)) decoder_31 (
    .out0(decoder_31_out0), .out1(decoder_31_out1), .out2(_3RB_RS[1]), .out3(_3RB_RS[2]),
    .sel(controlled_buffer_202_out), .en(and_27_out));
  or or_17 (_3RB_RS[0], decoder_31_out0, decoder_31_out1);
  assign controlled_buffer_226_out = and_28_out ? out_1[9:8] : 2'bz;  // Controlled_Buffer controlled_buffer_226
  Decoder #(.select(2), .disabled(0)) decoder_32 (
    .out0(decoder_32_out0), .out1(decoder_32_out1), .out2(_3RB_RS[1]), .out3(_3RB_RS[2]),
    .sel(controlled_buffer_226_out), .en(and_28_out));
  or or_18 (_3RB_RS[0], decoder_32_out0, decoder_32_out1);
  assign _3RB_FS = and_28_out ? 2'b01 : 2'bz;  // Controlled_Buffer controlled_buffer_227
  assign MuxBSel = and_28_out ? 2'b11 : 2'bz;  // Controlled_Buffer controlled_buffer_228
  assign ALUFS = and_28_out ? 4'b0110 : 4'bz;  // Controlled_Buffer controlled_buffer_229
  assign OutBSel = and_28_out ? out_1[3:2] : 2'bz;  // Controlled_Buffer controlled_buffer_230
  assign MuxCSel = and_28_out ? 1'b1 : 1'bz;  // Controlled_Buffer controlled_buffer_231
  assign OutASel = and_28_out ? out_1[6:5] : 2'bz;  // Controlled_Buffer controlled_buffer_232
  Hex_Digit_Display hex_digit_display_4 (.value(out_1[3:0]));  // open: dp
  and and_36 (and_36_out, SRCTDST, out_1[10], not_28_out);
  assign OutASel = and_36_out ? out_1[6:5] : 2'bz;  // Controlled_Buffer controlled_buffer_233
  assign MuxCSel = and_36_out ? 1'b1 : 1'bz;  // Controlled_Buffer controlled_buffer_234
  assign ALUFS = and_36_out ? 4'b0000 : 4'bz;  // Controlled_Buffer controlled_buffer_235
  assign MuxBSel = and_36_out ? 2'b11 : 2'bz;  // Controlled_Buffer controlled_buffer_236
  assign _3RB_FS = and_36_out ? 2'b01 : 2'bz;  // Controlled_Buffer controlled_buffer_237
  Decoder #(.select(2), .disabled(0)) decoder_33 (
    .out0(decoder_33_out0), .out1(decoder_33_out1), .out2(_3RB_RS[1]), .out3(_3RB_RS[2]),
    .sel(controlled_buffer_238_out), .en(and_36_out));
  assign controlled_buffer_238_out = and_36_out ? out_1[9:8] : 2'bz;  // Controlled_Buffer controlled_buffer_238
  or or_19 (_3RB_RS[0], decoder_33_out0, decoder_33_out1);
  assign IR_EN = IRLTPC ? 1'b1 : 1'bz;  // Controlled_Buffer controlled_buffer_239
  assign IR_LH = IRLTPC ? 1'b0 : 1'bz;  // Controlled_Buffer controlled_buffer_240
  assign MuxBSel = IRLTPC ? 2'b00 : 2'bz;  // Controlled_Buffer controlled_buffer_241
  assign _3RB_FS = IRLTPC ? 2'b01 : 2'bz;  // Controlled_Buffer controlled_buffer_242
  assign _3RB_RS = IRLTPC ? 4'b0001 : 4'bz;  // Controlled_Buffer controlled_buffer_243
  Decoder #(.select(2), .disabled(0)) decoder_34 (
    .out0(decoder_34_out0), .out1(decoder_34_out1), .out2(_3RB_RS[1]), .out3(_3RB_RS[2]),
    .sel(controlled_buffer_210_out), .en(and_35_out));
  or or_20 (_3RB_RS[0], decoder_34_out0, decoder_34_out1);
  outcdecoder outcdecoder_16 (.in_1(controlled_buffer_211_out), .out_2(OutCSel));
  Decoder #(.select(2)) decoder_35 (
    .out0(_4RB_RS[0]), .out1(_4RB_RS[1]), .out2(_4RB_RS[2]), .out3(_4RB_RS[3]),
    .sel(controlled_buffer_215_out), .en(IRTODST));
  and and_37 (and_37_out, NOT, out_1[7], out_1[10]);
  assign controlled_buffer_244_out = and_37_out ? out_1[6:5] : 2'bz;  // Controlled_Buffer controlled_buffer_244
  outcdecoder outcdecoder_17 (.in_1(controlled_buffer_244_out), .out_2(OutCSel));
  assign controlled_buffer_245_out = and_37_out ? out_1[9:8] : 2'bz;  // Controlled_Buffer controlled_buffer_245
  assign MuxCSel = and_37_out ? 1'b0 : 1'bz;  // Controlled_Buffer controlled_buffer_246
  assign ALUFS = and_37_out ? 4'b0010 : 4'bz;  // Controlled_Buffer controlled_buffer_247
  Controlled_Buffer #(.width(2)) controlled_buffer_248 (.out(MuxBSel), .en(and_37_out));  // open: in
  assign _3RB_FS = and_37_out ? 2'b01 : 2'bz;  // Controlled_Buffer controlled_buffer_249
  and and_38 (and_38_out, LSSRC, out_1[7], out_1[10]);
  outcdecoder outcdecoder_18 (.in_1(controlled_buffer_250_out), .out_2(OutCSel));
  assign controlled_buffer_250_out = and_38_out ? out_1[6:5] : 2'bz;  // Controlled_Buffer controlled_buffer_250
  assign controlled_buffer_251_out = and_38_out ? out_1[9:8] : 2'bz;  // Controlled_Buffer controlled_buffer_251
  assign MuxCSel = and_38_out ? 1'b0 : 1'bz;  // Controlled_Buffer controlled_buffer_252
  assign ALUFS = and_38_out ? 4'b1010 : 4'bz;  // Controlled_Buffer controlled_buffer_253
  assign MuxBSel = and_38_out ? 2'b11 : 2'bz;  // Controlled_Buffer controlled_buffer_254
  assign _3RB_FS = and_38_out ? 2'b01 : 2'bz;  // Controlled_Buffer controlled_buffer_255
  and and_39 (and_39_out, RSSRC, out_1[7], out_1[10]);
  assign controlled_buffer_256_out = and_39_out ? out_1[6:5] : 2'bz;  // Controlled_Buffer controlled_buffer_256
  outcdecoder outcdecoder_19 (.in_1(controlled_buffer_256_out), .out_2(OutCSel));
  assign controlled_buffer_257_out = and_39_out ? out_1[9:8] : 2'bz;  // Controlled_Buffer controlled_buffer_257
  assign MuxCSel = and_39_out ? 1'b0 : 1'bz;  // Controlled_Buffer controlled_buffer_258
  assign ALUFS = and_39_out ? 4'b1011 : 4'bz;  // Controlled_Buffer controlled_buffer_259
  assign MuxBSel = and_39_out ? 2'b11 : 2'bz;  // Controlled_Buffer controlled_buffer_260
  assign _3RB_FS = and_39_out ? 2'b01 : 2'bz;  // Controlled_Buffer controlled_buffer_261
  not not_28 (not_28_out, out_1[7]);
  and and_40 (and_40_out, SPTSRC, out_1[10]);
  assign controlled_buffer_262_out = and_40_out ? out_1[9:8] : 2'bz;  // Controlled_Buffer controlled_buffer_262
  Decoder #(.select(2), .disabled(0)) decoder_36 (
    .out0(decoder_36_out0), .out1(decoder_36_out1), .out2(_3RB_RS[1]), .out3(_3RB_RS[2]),
    .sel(controlled_buffer_262_out), .en(and_40_out));
  or or_21 (_3RB_RS[0], decoder_36_out0, decoder_36_out1);
  assign _3RB_FS = and_40_out ? 2'b01 : 2'bz;  // Controlled_Buffer controlled_buffer_263
  assign MuxBSel = and_40_out ? 2'b10 : 2'bz;  // Controlled_Buffer controlled_buffer_264
  Decoder #(.select(2), .disabled(0)) decoder_37 (
    .out0(decoder_37_out0), .out1(decoder_37_out1), .out2(_3RB_RS[1]), .out3(_3RB_RS[2]),
    .sel(controlled_buffer_245_out), .en(and_37_out));
  or or_22 (_3RB_RS[0], decoder_37_out0, decoder_37_out1);
  Decoder #(.select(2), .disabled(0)) decoder_38 (
    .out0(decoder_38_out0), .out1(decoder_38_out1), .out2(_3RB_RS[1]), .out3(_3RB_RS[2]),
    .sel(controlled_buffer_251_out), .en(and_38_out));
  or or_23 (_3RB_RS[0], decoder_38_out0, decoder_38_out1);
  Decoder #(.select(2), .disabled(0)) decoder_39 (
    .out0(decoder_39_out0), .out1(decoder_39_out1), .out2(_3RB_RS[1]), .out3(_3RB_RS[2]),
    .sel(controlled_buffer_257_out), .en(and_39_out));
  or or_24 (_3RB_RS[0], decoder_39_out0, decoder_39_out1);
  assign _3RB_FS = INCSP ? 2'b10 : 2'bz;  // Controlled_Buffer controlled_buffer_265
  assign _3RB_RS = INCSP ? 4'b0100 : 4'bz;  // Controlled_Buffer controlled_buffer_266
  and and_41 (and_41_out, ADD, not_31_out);
  not not_29 (not_29_out, out_1[10]);
  and and_42 (and_42_out, AND, not_29_out);
  not not_30 (not_30_out, out_1[10]);
  and and_43 (and_43_out, OR, not_30_out);
  not not_31 (not_31_out, out_1[10]);
  and and_44 (and_44_out, and_41_out, out_1[4]);
  and and_45 (and_45_out, and_42_out, out_1[7]);
  and and_46 (and_46_out, and_42_out, out_1[4]);
  and and_47 (and_47_out, and_43_out, out_1[4]);
  not not_32 (not_32_out, out_1[10]);
  and and_48 (and_48_out, SUB, not_32_out);
  and and_49 (and_49_out, and_48_out, out_1[4]);
  assign _3RB_FS = DECSP ? 2'b11 : 2'bz;  // Controlled_Buffer controlled_buffer_267
  assign _3RB_RS = DECSP ? 4'b0100 : 4'bz;  // Controlled_Buffer controlled_buffer_268
  and and_50 (and_50_out, and_41_out, out_1[7]);
  not not_33 (not_33_out, out_1[4]);
  not not_34 (not_34_out, out_1[7]);
  not not_35 (not_35_out, out_1[4]);
  and and_51 (and_51_out, and_43_out, out_1[7]);
  not not_36 (not_36_out, out_1[7]);
  not not_37 (not_37_out, out_1[4]);
  and and_52 (and_52_out, and_48_out, out_1[7]);
  outcdecoder outcdecoder_20 (.in_1(out_1[6:5]), .out_2(outcdecoder_20_out_2));
  and and_53 (and_53_out, and_41_out, not_38_out, not_33_out);
  not not_38 (not_38_out, out_1[7]);
  outcdecoder outcdecoder_21 (.in_1(out_1[3:2]), .out_2(outcdecoder_21_out_2));
  outcdecoder outcdecoder_22 (.in_1(out_1[6:5]), .out_2(outcdecoder_22_out_2));
  and and_54 (and_54_out, and_42_out, not_34_out, not_35_out);
  outcdecoder outcdecoder_23 (.in_1(out_1[3:2]), .out_2(outcdecoder_23_out_2));
  outcdecoder outcdecoder_24 (.in_1(out_1[6:5]), .out_2(outcdecoder_24_out_2));
  and and_55 (and_55_out, and_43_out, not_36_out, not_37_out);
  outcdecoder outcdecoder_25 (.in_1(out_1[3:2]), .out_2(outcdecoder_25_out_2));
  not not_39 (not_39_out, out_1[7]);
  not not_40 (not_40_out, out_1[4]);
  Decoder #(.select(2)) decoder_40 (
    .out0(_4RB_RS[0]), .out1(_4RB_RS[1]), .out2(_4RB_RS[2]), .out3(_4RB_RS[3]),
    .sel(controlled_buffer_269_out), .en(and_50_out));
  assign controlled_buffer_269_out = and_50_out ? out_1[9:8] : 2'bz;  // Controlled_Buffer controlled_buffer_269
  assign _4RB_FS = and_50_out ? 2'b01 : 2'bz;  // Controlled_Buffer controlled_buffer_270
  assign ALUFS = and_50_out ? 4'b0100 : 4'bz;  // Controlled_Buffer controlled_buffer_271
  assign MuxASel = and_50_out ? 2'b11 : 2'bz;  // Controlled_Buffer controlled_buffer_272
  assign OutBSel = and_50_out ? out_1[3:2] : 2'bz;  // Controlled_Buffer controlled_buffer_273
  assign OutCSel = and_50_out ? outcdecoder_20_out_2 : 2'bz;  // Controlled_Buffer controlled_buffer_274
  assign MuxCSel = and_50_out ? 1'b0 : 1'bz;  // Controlled_Buffer controlled_buffer_275
  assign ALUFS = and_44_out ? 4'b0100 : 4'bz;  // Controlled_Buffer controlled_buffer_276
  assign MuxASel = and_44_out ? 2'b11 : 2'bz;  // Controlled_Buffer controlled_buffer_277
  assign OutBSel = and_44_out ? out_1[6:5] : 2'bz;  // Controlled_Buffer controlled_buffer_278
  assign OutCSel = and_44_out ? outcdecoder_21_out_2 : 2'bz;  // Controlled_Buffer controlled_buffer_279
  assign MuxCSel = and_44_out ? 1'b0 : 1'bz;  // Controlled_Buffer controlled_buffer_280
  assign _4RB_FS = and_44_out ? 2'b01 : 2'bz;  // Controlled_Buffer controlled_buffer_281
  Decoder #(.select(2)) decoder_41 (
    .out0(_4RB_RS[0]), .out1(_4RB_RS[1]), .out2(_4RB_RS[2]), .out3(_4RB_RS[3]),
    .sel(controlled_buffer_282_out), .en(and_44_out));
  assign controlled_buffer_282_out = and_44_out ? out_1[9:8] : 2'bz;  // Controlled_Buffer controlled_buffer_282
  Decoder #(.select(2)) decoder_42 (
    .out0(_4RB_RS[0]), .out1(_4RB_RS[1]), .out2(_4RB_RS[2]), .out3(_4RB_RS[3]),
    .sel(controlled_buffer_283_out), .en(and_45_out));
  assign controlled_buffer_283_out = and_45_out ? out_1[9:8] : 2'bz;  // Controlled_Buffer controlled_buffer_283
  assign _4RB_FS = and_45_out ? 2'b01 : 2'bz;  // Controlled_Buffer controlled_buffer_284
  assign ALUFS = and_45_out ? 4'b0111 : 4'bz;  // Controlled_Buffer controlled_buffer_285
  assign MuxASel = and_45_out ? 2'b11 : 2'bz;  // Controlled_Buffer controlled_buffer_286
  assign OutBSel = and_45_out ? out_1[3:2] : 2'bz;  // Controlled_Buffer controlled_buffer_287
  assign OutCSel = and_45_out ? outcdecoder_22_out_2 : 2'bz;  // Controlled_Buffer controlled_buffer_288
  assign MuxCSel = and_45_out ? 1'b0 : 1'bz;  // Controlled_Buffer controlled_buffer_289
  assign ALUFS = and_46_out ? 4'b0111 : 4'bz;  // Controlled_Buffer controlled_buffer_290
  assign MuxASel = and_46_out ? 2'b11 : 2'bz;  // Controlled_Buffer controlled_buffer_291
  assign OutBSel = and_46_out ? out_1[6:5] : 2'bz;  // Controlled_Buffer controlled_buffer_292
  assign OutCSel = and_46_out ? outcdecoder_23_out_2 : 2'bz;  // Controlled_Buffer controlled_buffer_293
  assign MuxCSel = and_46_out ? 1'b0 : 1'bz;  // Controlled_Buffer controlled_buffer_294
  assign _4RB_FS = and_46_out ? 2'b01 : 2'bz;  // Controlled_Buffer controlled_buffer_295
  assign controlled_buffer_296_out = and_46_out ? out_1[9:8] : 2'bz;  // Controlled_Buffer controlled_buffer_296
  Decoder #(.select(2)) decoder_43 (
    .out0(_4RB_RS[0]), .out1(_4RB_RS[1]), .out2(_4RB_RS[2]), .out3(_4RB_RS[3]),
    .sel(controlled_buffer_296_out), .en(and_46_out));
  Decoder #(.select(2)) decoder_44 (
    .out0(_4RB_RS[0]), .out1(_4RB_RS[1]), .out2(_4RB_RS[2]), .out3(_4RB_RS[3]),
    .sel(controlled_buffer_297_out), .en(and_51_out));
  assign controlled_buffer_297_out = and_51_out ? out_1[9:8] : 2'bz;  // Controlled_Buffer controlled_buffer_297
  assign _4RB_FS = and_51_out ? 2'b01 : 2'bz;  // Controlled_Buffer controlled_buffer_298
  assign ALUFS = and_51_out ? 4'b1000 : 4'bz;  // Controlled_Buffer controlled_buffer_299
  assign MuxASel = and_51_out ? 2'b11 : 2'bz;  // Controlled_Buffer controlled_buffer_300
  assign OutBSel = and_51_out ? out_1[3:2] : 2'bz;  // Controlled_Buffer controlled_buffer_301
  assign OutCSel = and_51_out ? outcdecoder_24_out_2 : 2'bz;  // Controlled_Buffer controlled_buffer_302
  assign MuxCSel = and_51_out ? 1'b0 : 1'bz;  // Controlled_Buffer controlled_buffer_303
  assign ALUFS = and_47_out ? 4'b1000 : 4'bz;  // Controlled_Buffer controlled_buffer_304
  assign MuxASel = and_47_out ? 2'b11 : 2'bz;  // Controlled_Buffer controlled_buffer_305
  assign OutBSel = and_47_out ? out_1[6:5] : 2'bz;  // Controlled_Buffer controlled_buffer_306
  assign OutCSel = and_47_out ? outcdecoder_25_out_2 : 2'bz;  // Controlled_Buffer controlled_buffer_307
  assign MuxCSel = and_47_out ? 1'b0 : 1'bz;  // Controlled_Buffer controlled_buffer_308
  assign _4RB_FS = and_47_out ? 2'b01 : 2'bz;  // Controlled_Buffer controlled_buffer_309
  Decoder #(.select(2)) decoder_45 (
    .out0(_4RB_RS[0]), .out1(_4RB_RS[1]), .out2(_4RB_RS[2]), .out3(_4RB_RS[3]),
    .sel(controlled_buffer_310_out), .en(and_47_out));
  assign controlled_buffer_310_out = and_47_out ? out_1[9:8] : 2'bz;  // Controlled_Buffer controlled_buffer_310
  assign controlled_buffer_311_out = and_52_out ? out_1[9:8] : 2'bz;  // Controlled_Buffer controlled_buffer_311
  assign _4RB_FS = and_52_out ? 2'b01 : 2'bz;  // Controlled_Buffer controlled_buffer_312
  assign ALUFS = and_52_out ? 4'b0110 : 4'bz;  // Controlled_Buffer controlled_buffer_313
  assign MuxASel = and_52_out ? 2'b11 : 2'bz;  // Controlled_Buffer controlled_buffer_314
  assign OutBSel = and_52_out ? out_1[3:2] : 2'bz;  // Controlled_Buffer controlled_buffer_315
  outcdecoder outcdecoder_26 (.in_1(out_1[6:5]), .out_2(outcdecoder_26_out_2));
  assign OutCSel = and_52_out ? outcdecoder_26_out_2 : 2'bz;  // Controlled_Buffer controlled_buffer_316
  assign MuxCSel = and_52_out ? 1'b0 : 1'bz;  // Controlled_Buffer controlled_buffer_317
  and and_56 (and_56_out, and_48_out, not_39_out, not_40_out);
  assign ALUFS = and_49_out ? 4'b0110 : 4'bz;  // Controlled_Buffer controlled_buffer_318
  assign MuxASel = and_49_out ? 2'b11 : 2'bz;  // Controlled_Buffer controlled_buffer_319
  assign OutBSel = and_49_out ? out_1[6:5] : 2'bz;  // Controlled_Buffer controlled_buffer_320
  outcdecoder outcdecoder_27 (.in_1(out_1[3:2]), .out_2(outcdecoder_27_out_2));
  assign OutCSel = and_49_out ? outcdecoder_27_out_2 : 2'bz;  // Controlled_Buffer controlled_buffer_321
  assign MuxCSel = and_49_out ? 1'b0 : 1'bz;  // Controlled_Buffer controlled_buffer_322
  assign _4RB_FS = and_49_out ? 2'b01 : 2'bz;  // Controlled_Buffer controlled_buffer_323
  assign controlled_buffer_324_out = and_49_out ? out_1[9:8] : 2'bz;  // Controlled_Buffer controlled_buffer_324
  Decoder #(.select(2)) decoder_46 (
    .out0(_4RB_RS[0]), .out1(_4RB_RS[1]), .out2(_4RB_RS[2]), .out3(_4RB_RS[3]),
    .sel(controlled_buffer_311_out), .en(and_52_out));
  Decoder #(.select(2)) decoder_47 (
    .out0(_4RB_RS[0]), .out1(_4RB_RS[1]), .out2(_4RB_RS[2]), .out3(_4RB_RS[3]),
    .sel(controlled_buffer_324_out), .en(and_49_out));
  assign controlled_buffer_325_out = and_53_out ? out_1[9:8] : 2'bz;  // Controlled_Buffer controlled_buffer_325
  Decoder #(.select(2)) decoder_48 (
    .out0(_4RB_RS[0]), .out1(_4RB_RS[1]), .out2(_4RB_RS[2]), .out3(_4RB_RS[3]),
    .sel(controlled_buffer_325_out), .en(and_53_out));
  assign _4RB_FS = and_53_out ? 2'b01 : 2'bz;  // Controlled_Buffer controlled_buffer_326
  assign MuxASel = and_53_out ? 2'b11 : 2'bz;  // Controlled_Buffer controlled_buffer_327
  assign ALUFS = and_53_out ? 4'b0100 : 4'bz;  // Controlled_Buffer controlled_buffer_328
  assign OutBSel = and_53_out ? out_1[3:2] : 2'bz;  // Controlled_Buffer controlled_buffer_329
  assign MuxCSel = and_53_out ? 1'b1 : 1'bz;  // Controlled_Buffer controlled_buffer_330
  assign OutASel = and_53_out ? out_1[6:5] : 2'bz;  // Controlled_Buffer controlled_buffer_331
  Decoder #(.select(2)) decoder_49 (
    .out0(_4RB_RS[0]), .out1(_4RB_RS[1]), .out2(_4RB_RS[2]), .out3(_4RB_RS[3]),
    .sel(controlled_buffer_332_out), .en(and_54_out));
  assign controlled_buffer_332_out = and_54_out ? out_1[9:8] : 2'bz;  // Controlled_Buffer controlled_buffer_332
  assign _4RB_FS = and_54_out ? 2'b01 : 2'bz;  // Controlled_Buffer controlled_buffer_333
  assign MuxASel = and_54_out ? 2'b11 : 2'bz;  // Controlled_Buffer controlled_buffer_334
  assign ALUFS = and_54_out ? 4'b0111 : 4'bz;  // Controlled_Buffer controlled_buffer_335
  assign OutBSel = and_54_out ? out_1[3:2] : 2'bz;  // Controlled_Buffer controlled_buffer_336
  assign MuxCSel = and_54_out ? 1'b1 : 1'bz;  // Controlled_Buffer controlled_buffer_337
  assign OutASel = and_54_out ? out_1[6:5] : 2'bz;  // Controlled_Buffer controlled_buffer_338
  assign controlled_buffer_339_out = and_55_out ? out_1[9:8] : 2'bz;  // Controlled_Buffer controlled_buffer_339
  Decoder #(.select(2)) decoder_50 (
    .out0(_4RB_RS[0]), .out1(_4RB_RS[1]), .out2(_4RB_RS[2]), .out3(_4RB_RS[3]),
    .sel(controlled_buffer_339_out), .en(and_55_out));
  assign _4RB_FS = and_55_out ? 2'b01 : 2'bz;  // Controlled_Buffer controlled_buffer_340
  assign MuxASel = and_55_out ? 2'b11 : 2'bz;  // Controlled_Buffer controlled_buffer_341
  assign ALUFS = and_55_out ? 4'b1000 : 4'bz;  // Controlled_Buffer controlled_buffer_342
  assign OutBSel = and_55_out ? out_1[3:2] : 2'bz;  // Controlled_Buffer controlled_buffer_343
  assign MuxCSel = and_55_out ? 1'b1 : 1'bz;  // Controlled_Buffer controlled_buffer_344
  assign OutASel = and_55_out ? out_1[6:5] : 2'bz;  // Controlled_Buffer controlled_buffer_345
  assign controlled_buffer_346_out = and_56_out ? out_1[9:8] : 2'bz;  // Controlled_Buffer controlled_buffer_346
  assign _4RB_FS = and_56_out ? 2'b01 : 2'bz;  // Controlled_Buffer controlled_buffer_347
  assign MuxASel = and_56_out ? 2'b11 : 2'bz;  // Controlled_Buffer controlled_buffer_348
  assign ALUFS = and_56_out ? 4'b0110 : 4'bz;  // Controlled_Buffer controlled_buffer_349
  assign OutBSel = and_56_out ? out_1[3:2] : 2'bz;  // Controlled_Buffer controlled_buffer_350
  assign MuxCSel = and_56_out ? 1'b1 : 1'bz;  // Controlled_Buffer controlled_buffer_351
  assign OutASel = and_56_out ? out_1[6:5] : 2'bz;  // Controlled_Buffer controlled_buffer_352
  Decoder #(.select(2)) decoder_51 (
    .out0(_4RB_RS[0]), .out1(_4RB_RS[1]), .out2(_4RB_RS[2]), .out3(_4RB_RS[3]),
    .sel(controlled_buffer_346_out), .en(and_56_out));

  // Other names for the same wires on the sheet: ADDRESS[7:0] = out_1[7:0]; INSTR[15:0] = out_1;
  //   SRCREG2[2:0] = out_1[4:2]; SRCREG1[2:0] = out_1[7:5]; AdrMOD = out_1[8]; DESTREG[2:0] = out_1[10:8];
  //   REGSEL[1:0] = out_1[10:9]; OPCODE[4:0] = out_1[15:11]

  // Notes on the sheet:
  //   MARTIRL
  //   OR (DEST IN 3RB)
  //   MARTIRH
  //   INC
  //   MTDST
  //   SRCTSP
  //   ADD (DEST IN 3RB)
  //   SUB (DEST IN 3RB)
  //   AND (DEST IN 3RB)
  //   SRCTODST
  //   NOT
  //   LSSRC
  //   RSSRC
  //   Memory Independent Operations
  //   SRCTOM
  //   DEC
  //   IRTODST
  //   SPTSRC
  //   IRLTPC
  //   INCSP
  //   ADD (DEST IN 4RB)
  //   AND (DEST IN 4RB)
  //   OR (DEST IN 4RB)
  //   DECSP
  //   SUB (DEST IN 4RB)
endmodule

module CONTROL_UNIT (
  input  in_1,
  input  in_2,
  input  NEGATIVE_FLAG,
  input  ZERO_FLAG,
  input  [4:0] OPCODE,
  output [2:0] F1,
  output [2:0] F2,
  output [2:0] F3
);

  wire and_1_out, and_2_out, and_3_out, and_4_out, decoder_1_out0, decoder_1_out1, decoder_1_out2,
       decoder_1_out3, multiplexer_1_out, not_1_out, not_2_out;
  wire [1:0] rom_1_data_3, rom_1_data_4;
  wire [2:0] rom_1_data;
  wire [7:0] adder_1_out, controlled_buffer_1_out, controlled_buffer_4_out, register_1_q, register_2_q,
       rom_1_data_2;
  wire [7:2] adder_2_out;

  not not_1 (not_1_out, multiplexer_1_out);
  and and_1 (and_1_out, decoder_1_out0, not_1_out);
  Adder adder_1 (.a(register_1_q), .b(8'h1), .out(adder_1_out));  // open: cin, cout
  assign controlled_buffer_1_out = and_1_out ? adder_1_out : 8'bz;  // Controlled_Buffer controlled_buffer_1
  and and_2 (and_2_out, decoder_1_out0, multiplexer_1_out);
  assign controlled_buffer_1_out = and_2_out ? rom_1_data_2 : 8'bz;  // Controlled_Buffer controlled_buffer_2
  and and_3 (and_3_out, decoder_1_out1, multiplexer_1_out);
  assign controlled_buffer_1_out = and_3_out ? rom_1_data_2 : 8'bz;  // Controlled_Buffer controlled_buffer_3
  assign controlled_buffer_4_out = and_3_out ? adder_1_out : 8'bz;  // Controlled_Buffer controlled_buffer_4
  not not_2 (not_2_out, multiplexer_1_out);
  and and_4 (and_4_out, decoder_1_out1, not_2_out);
  assign controlled_buffer_1_out = and_4_out ? adder_1_out : 8'bz;  // Controlled_Buffer controlled_buffer_5
  Register register_1 (.D(controlled_buffer_1_out), .Q(register_1_q), .clk(in_1));  // open: en, clr
  Register register_2 (.D(controlled_buffer_4_out), .en(and_3_out), .Q(register_2_q), .clk(in_1));  // open: clr
  assign controlled_buffer_1_out = decoder_1_out2 ? register_2_q : 8'bz;  // Controlled_Buffer controlled_buffer_6
  assign controlled_buffer_1_out = decoder_1_out3 ? {adder_2_out, 2'b00} : 8'bz;  // Controlled_Buffer controlled_buffer_7
  ROM #(.dataWidth(24)) rom_1 (
    .addr(register_1_q), .data({F1, F2, F3, rom_1_data_4, rom_1_data_3, rom_1_data_2, rom_1_data}));  // open: sel
  Decoder #(.select(2), .enable("false")) decoder_1 (
    .out0(decoder_1_out0), .out1(decoder_1_out1), .out2(decoder_1_out2), .out3(decoder_1_out3),
    .sel(rom_1_data_3));
  Multiplexer #(.select(2), .enable("false")) multiplexer_1 (
    .in0(1'b1), .in1(in_2), .in2(NEGATIVE_FLAG), .in3(ZERO_FLAG), .out(multiplexer_1_out), .sel(rom_1_data_4));
  Adder #(.width(5)) adder_2 (.a(OPCODE), .b(5'b00001), .out(adder_2_out[6:2]), .cout(adder_2_out[7]));  // open: cin

  // Notes on the sheet:
  //   Control Unit
  //   CAR
  //   SP
  //   Control Memory
  //   contents of rom_1 (hex, n*v repeats v):
  //   8008 10010 1800 0 402000 600000 0 0 e00000 0 0 0 200000 0 0 0 18088 38000 0 0 300a8 20000 0 0 40000
  //   0 0 0 a00000 0 0 0 200108 c00000 0 0 200128 800000 10*0 100000 0 0 0 140000 0 0 0 180000 0 0 0 28000
  //   0 0 0 6210 0 28000 0 2e000 0 0 0 18248 38250 28000 0 30268 20000
  //   IR LOW PLACEHOLDER
endmodule

module outcdecoder (
  input  [1:0] in_1,
  output [1:0] out_2
);

  Subtractor #(.width(2)) subtractor_1 (.a(in_1), .b(2'b01), .out(out_2));  // open: bin, bout
endmodule

module converter (
  input  [4:0] OPCode,
  input  [1:0] RegSel,
  input  Adressing_Mode,
  input  [7:0] Address,
  input  Type_1,
  input  [4:0] OPCode_2,
  input  [2:0] DestReg,
  input  [2:0] SrcReg1,
  input  [2:0] SrcReg2,
  input  [2:0] F1,
  input  [2:0] F2,
  input  [2:0] F3,
  input  [1:0] CD,
  input  [2:0] FILLER,
  input  [1:0] BR,
  input  [7:0] AD
);

  wire not_1_out;
  wire [15:0] controlled_buffer_1_out;

  assign controlled_buffer_1_out = Type_1 ? {OPCode, RegSel, Adressing_Mode, Address} : 16'bz;  // Controlled_Buffer controlled_buffer_1
  not not_1 (not_1_out, Type_1);
  assign controlled_buffer_1_out = not_1_out ? {OPCode_2, DestReg, SrcReg1, SrcReg2, 2'b00} : 16'bz;  // Controlled_Buffer controlled_buffer_2
  // Probe on controlled_buffer_1_out[15:8]
  // Probe on controlled_buffer_1_out[7:0]
  // Probe on {F1, F2, F3, CD, BR, AD, FILLER}
endmodule
